// Logisim project MIPS32.circ as structural Verilog
module MIPS32 (
);

  wire c1_out;
  wire [1:0] PC_q;
  wire [29:0] incrementer_1_p2, PC_q_2;
  wire [31:0] ALUresult1_q, MEMdata_q, mipsprogramrom_1_p2, mipsprogramrom_1_p3, PC4DE_q, PC4EM_q, PC4FD_q,
       WBdata;

  Clock c1 (.out(c1_out));
  Register #(.width(32), .trigger("falling")) PC (
    .D({incrementer_1_p2, PC_q}), .clk(c1_out), .Q({PC_q_2, PC_q}));  // open: en, clr
  // Incrementer #(.width(30)) incrementer_1: pin names not known; wires that end beside it: PC_q_2, incrementer_1_p2
  // MIPSProgramROM mipsprogramrom_1: pin names not known; wires that end beside it: {PC_q_2, PC_q}, mipsprogramrom_1_p2, mipsprogramrom_1_p3
  Register #(.width(32), .trigger("falling")) PC4FD (
    .D({incrementer_1_p2, PC_q}), .clk(c1_out), .Q(PC4FD_q));  // open: en, clr
  Register #(.width(32), .trigger("falling")) Instruction (
    .D(mipsprogramrom_1_p2), .clk(c1_out), .Q(mipsprogramrom_1_p3));  // open: en, clr
  // RegisterFile registerfile_1: pin names not known; wires that end beside it: WBdata, mipsprogramrom_1_p3[25:21], mipsprogramrom_1_p3[20:16]
  Register #(.width(32), .trigger("falling")) PC4DE (.D(PC4FD_q), .clk(c1_out), .Q(PC4DE_q));  // open: en, clr
  Register #(.width(32), .trigger("falling")) A (.clk(c1_out));  // open: D, en, Q, clr
  Register #(.width(32), .trigger("falling")) B (.clk(c1_out));  // open: D, en, Q, clr
  Register #(.width(32), .trigger("falling")) Imm (.clk(c1_out));  // open: D, en, Q, clr
  Register #(.width(32), .trigger("falling")) Rd (.clk(c1_out));  // open: D, en, Q, clr
  Register #(.width(32), .trigger("falling")) Rt (.clk(c1_out));  // open: D, en, Q, clr
  Register #(.width(4), .trigger("falling")) EXCtrl (.clk(c1_out));  // open: D, en, Q, clr
  Register #(.width(3), .trigger("falling")) MEMCtrl0 (.clk(c1_out));  // open: D, en, Q, clr
  Register #(.width(3), .trigger("falling")) WBCtrl0 (.clk(c1_out));  // open: D, en, Q, clr
  // Mips_ALU mips_alu_1: pin names not known
  Register #(.width(32), .trigger("falling")) PC4EM (.D(PC4DE_q), .clk(c1_out), .Q(PC4EM_q));  // open: en, clr
  Register #(.width(32), .trigger("falling")) ALUresult0 (.clk(c1_out));  // open: D, en, Q, clr
  Register #(.width(32), .trigger("falling")) Dest0 (.clk(c1_out));  // open: D, en, Q, clr
  Register #(.width(3), .trigger("falling")) MEMCtrl1 (.clk(c1_out));  // open: D, en, Q, clr
  Register #(.width(3), .trigger("falling")) WBCtrl1 (.clk(c1_out));  // open: D, en, Q, clr
  Register #(.width(32), .trigger("falling")) PC4MW (.D(PC4EM_q), .clk(c1_out));  // open: en, Q, clr
  Register #(.width(32), .trigger("falling")) ALUresult1 (.clk(c1_out), .Q(ALUresult1_q));  // open: D, en, clr
  Register #(.width(32), .trigger("falling")) MEMdata (.clk(c1_out), .Q(MEMdata_q));  // open: D, en, clr
  Register #(.width(32), .trigger("falling")) Dest1 (.clk(c1_out));  // open: D, en, Q, clr
  Register #(.width(3), .trigger("falling")) WBCtrl2 (.clk(c1_out));  // open: D, en, Q, clr
  Multiplexer #(.width(32), .enable("false")) multiplexer_1 (
    .in0(ALUresult1_q), .in1(MEMdata_q), .out(WBdata));  // open: sel

  // Notes on the sheet:
  //   IF stage
  //   contents of mipsprogramrom_1 (hex, n*v repeats v):
  //   ADDIU $1,$10,-1001 ANDI $10,$10,1001 ORI $10,$10,1001 XORI $10,$10,1001
  //   ID stage
  //   EX stage
  //   MEM stage
  //   WB stage
endmodule

module Control (
  input  in_1,
  input  in_2,
  input  in_3,
  input  in_4,
  input  in_5,
  input  in_6,
  output out_7,
  output out_8,
  output out_9,
  output out_10,
  output out_11,
  output out_12,
  output out_13,
  output out_14,
  output out_15
);
endmodule
